# Fritzing sketch calc (saved by Fritzing 0.9.2b)
breadboards: 1

parts:
  7_Segment_4_Digit_Display1 = 7-SEGMENT-4DIGIT common anode [part_number="5461BS - 5462BS" package=7-segment-4digit-anode]
  パーツ1 = Arduino Uno (Rev3)
  R1 = Resistor [tolerance=±5% resistance=220 package=THT]
  R2 = Resistor [tolerance=±5% resistance=220 package=THT]
  R3 = Resistor [tolerance=±0.05% resistance=220 package=THT]
  R4 = Resistor [tolerance=±5% resistance=220 package=THT]
  Matrix_keypad1 = KEYPAD 4x4

nets:
  N1: 7_Segment_4_Digit_Display1.pin_1, パーツ1.D2
  N2: 7_Segment_4_Digit_Display1.pin_2, パーツ1.D3_PWM
  N3: 7_Segment_4_Digit_Display1.pin_3, パーツ1.D4
  N4: 7_Segment_4_Digit_Display1.pin_4, パーツ1.D5_PWM
  N5: 7_Segment_4_Digit_Display1.pin_5, パーツ1.D6_PWM
  N6: 7_Segment_4_Digit_Display1.pin_6, R2.Pin_0
  N7: 7_Segment_4_Digit_Display1.pin_7, パーツ1.D8
  N8: 7_Segment_4_Digit_Display1.pin_8, R4.Pin_0
  N9: 7_Segment_4_Digit_Display1.pin_9, R3.Pin_0
  N10: 7_Segment_4_Digit_Display1.pin_10, パーツ1.D11_PWM/MOSI
  N11: 7_Segment_4_Digit_Display1.pin_11, パーツ1.D12/MISO
  N12: 7_Segment_4_Digit_Display1.pin_12, R1.Pin_0
  N13: パーツ1.A0, Matrix_keypad1.row4
  N14: パーツ1.A1, Matrix_keypad1.row3
  N15: パーツ1.A2, Matrix_keypad1.row2
  N16: パーツ1.A3, Matrix_keypad1.row1
  N17: パーツ1.A4/SDA, Matrix_keypad1.col4
  N18: パーツ1.A5/SCL, Matrix_keypad1.col3
  N19: パーツ1.D9_PWM, R4.Pin_1
  N20: パーツ1.D10_PWM/SS, R3.Pin_1
  N21: パーツ1.D13/SCK, R1.Pin_1
  N22: パーツ1.D0/RX, Matrix_keypad1.col1
  N23: パーツ1.D1/TX, Matrix_keypad1.col2
  N24: パーツ1.D7, R2.Pin_1

notes:
  7 segment 4 digtis display
  3461BS
  PARALLAX 27899
  4x4 Matrix Membrane Keypad

custom parts:
  7-SEGMENT-4DIGIT common anode: A 7 Segment 4 Digit common anode display, with decimal points
  KEYPAD 4x4: Matrix keypad 16 buttons, 4 rows x 4 columns
